# Fritzing sketch aquaMonitor (saved by Fritzing 0.9.3b)
breadboards: 1

parts:
  Composant1 = Arduino GSM Shield
  U1 = POT [part_number=P1 package=pot_alpha_rv16af-20]
  U2 = LCD-16X2 [part_number=LCD package=lcd-16x2_noholes]
  Composant3 = Real Time Clock Module - DS1307 RTC Breakout Board [part_number=RTC]
  U3 = TEMPERATURE-SENSOR [part_number=DS18B20 package=to-92]
  R1 = PHOTOCELL [part_number=LDR package=photocell]
  S1 = Floater Switch
  D1 = Rectifier Diode [part_number=1N4001 package="300 mil [THT]"]
  BAT1 = BC9VPC [package=bc9vpc]
  R5 = Resistor [tolerance=±5% resistance=470k package=THT]
  R4 = Resistor [tolerance=±5% resistance=220k package=THT]
  R3 = Resistor [tolerance=±5% resistance=4.7k package=THT]
  R2 = Resistor [tolerance=±5% resistance=10k package=THT]
  Composant4 = Arduino Mega ADK (Rev3)
  U4 = ESP8266 WiFi Module [part_number=ESP8266]  # not connected
  Composant5 = Logic Level Converter

nets:
  N1: Composant1.A5/SCL, Composant3.SCL
  N2: Composant1.A4/SDA, Composant3.SDA
  GND: Composant1.AGND, U1.A, U2.VSS, U2.R_W, U2.K, Composant3.GND, U3.GND, S1.leg0, BAT1.V-, R4.Pin_0, R2.Pin_1
  N3: Composant1.SCK/D13, U2.DB7
  N4: Composant1.MISO/D12, U3.VCC, R3.Pin_1
  N5: Composant1.MOSI/PWM_D11, S1.leg1
  N6: Composant1.SS/PWM_D10, Composant1.DSM_RX_D2
  N7: Composant1.PWM_D9, U2.DB6
  N8: Composant1.D8, U2.DB5
  5V: Composant1.5V, U2.VDD, U2.A, Composant3.5V, U3.ADJ, R1.P$2, R3.Pin_0
  N9: Composant1.VIN, D1.cathode
  N10: Composant1.PWM_D4, U2.RS
  N11: Composant1.PWM_D5, U2.E
  N12: Composant1.PWM_D6, U2.DB4
  N13: Composant1.A0, R1.P$1, R2.Pin_0
  N14: Composant1.A1, R5.Pin_0, R4.Pin_1
  N15: U1.S, U2.VO
  N16: D1.anode, BAT1.V+
  N17: Composant4.D19/RX1, Composant5.TX_HV
  N18: Composant4.D18/TX1, Composant5.RX_HV

notes:
  +VCC (12V)
  These two resistors mounted directly under Arduino PCB on main power jack pins
  GSM module pin2 must not be connected to arduino pin2.
  Cut off the pin on intermediate pcb

custom parts:
  Floater Switch: Water level switch
  ESP8266 WiFi Module: Generic WiFi Module based on the ESP8266 with onboard PCB antenna and UART communications
