# Fritzing sketch pcb0 (saved by Fritzing 0.9.3b)
circuit board: 5.3353cm x 5.3cm
breadboards: 1

parts:
  Level = female pin header, 2 pins [form="♀ (female)" part_number=Level]
  Temp = female pin header, 3 pins [form="♀ (female)" part_number=Temp]
  Composant1 = Arduino Uno (Rev3)
  R2 = Resistor [tolerance=±5% resistance=220 package=THT]
  R3 = Resistor [tolerance=±5% resistance=220 package=THT]
  RTC = female pin header, 4 pins [form="♀ (female)" part_number=RTC]
  Light = female pin header, 2 pins [form="♀ (female)" part_number=Light]
  R4 = Resistor [tolerance=±5% resistance=220 package=THT]
  Bat = female pin header, 2 pins [form="♀ (female)" part_number=Battery]
  R5 = Trimmer Potentiometer [maximum_resistance=10kΩ package=THT]
  LCD = female pin header, 9 pins [form="♀ (female)"]
  Reset = female pin header, 2 pins [form="♀ (female)" part_number=Reset]
  D1-1 = female pin header, 1 pin [form="♀ (female)"]
  D1-2 = female pin header, 1 pin [form="♀ (female)"]

nets:
  N1: Level.pin1, Temp.pin2, Composant1.GND, RTC.pin4, R4.Pin_1, Bat.pin2, R5.wiper, LCD.pin1, Reset.pin2
  N2: Level.pin2, Composant1.D11_PWM/MOSI
  N3: Temp.pin1, Composant1.5V, R2.Pin_1, R3.Pin_1, RTC.pin3, Light.pin1, LCD.pin2
  N4: Temp.pin3, Composant1.D12/MISO, R2.Pin_0, R3.Pin_0
  N5: Composant1.A0, Light.pin2, R4.Pin_0
  N6: Composant1.A4/SDA, RTC.pin2
  N7: Composant1.A5/SCL, RTC.pin1
  N8: Composant1.D8, LCD.pin6
  N9: Composant1.D9_PWM, LCD.pin5
  N10: Composant1.D10_PWM/SS, Composant1.D2
  N11: Composant1.D13/SCK, LCD.pin4
  N12: Composant1.D4, LCD.pin9
  N13: Composant1.D5_PWM, LCD.pin8
  N14: Composant1.D6_PWM, LCD.pin7
  N15: Composant1.RESET, Reset.pin1
  N16: Composant1.VIN, D1-2.pin1
  N17: Bat.pin1, D1-1.pin1
  N18: R5.leg1, LCD.pin3

notes:
  @reivax
  Aquamonitor
  +
